# Fritzing sketch 04_led (saved by Fritzing 0.9.10b)
breadboards: 1

parts:
  LED1 = LED - 5mm [color="Red (633nm)" current=0.030 package="5 mm [THT]"]
  R1 = Resistor [tolerance=±5% power=0.25 resistance=220 package=THT]
  부품1 = Arduino Uno (Rev3)

nets:
  N1: LED1.cathode, 부품1.GND
  N2: LED1.anode, R1.Pin_0
  N3: R1.Pin_1, 부품1.D2
